# Fritzing sketch Arduino_POD_Midi_Switch_Arduino_Nano (saved by Fritzing 0.9.3b)
circuit board: 9cm x 7cm
breadboards: 1

parts:
  R1 = Resistor [tolerance=±5% resistance=10k package=THT]
  S1 = Pushbutton [package="[THT]"]
  R2 = Resistor [tolerance=±5% resistance=10k package=THT]
  R3 = Resistor [tolerance=±5% resistance=220 package=THT]
  LED1 = LED - 5mm [color="Red (633nm)" package="5 mm [THT]"]
  R4 = Resistor [tolerance=±5% resistance=10k package=THT]
  S2 = Pushbutton [package="[THT]"]
  R5 = Resistor [tolerance=±5% resistance=10k package=THT]
  R6 = Resistor [tolerance=±5% resistance=220 package=THT]
  LED2 = LED - 5mm [color="Red (633nm)" package="5 mm [THT]"]
  R7 = Resistor [tolerance=±5% resistance=10k package=THT]
  R8 = Resistor [tolerance=±5% resistance=10k package=THT]
  S3 = Pushbutton [package="[THT]"]
  S4 = Pushbutton [package="[THT]"]
  R9 = Resistor [tolerance=±5% resistance=10k package=THT]
  R10 = Resistor [tolerance=±5% resistance=10k package=THT]
  R11 = Resistor [tolerance=±5% resistance=220 package=THT]
  R12 = Resistor [tolerance=±5% resistance=220 package=THT]
  LED3 = LED - 5mm [color="Red (633nm)" package="5 mm [THT]"]
  LED4 = LED - 5mm [color="Red (633nm)" package="5 mm [THT]"]
  DIN1 = DIN-5 jack (MIDI) [package=THT]
  R13 = Resistor [tolerance=±5% resistance=220 package=THT]
  Bauteil2 = Arduino Nano (Rev3.0)

nets:
  N1: R1.Pin_0, R4.Pin_0, R7.Pin_0, R8.Pin_0, R13.Pin_1, Bauteil2.5V
  N2: R1.Pin_1, S1.Pin_3, S1.Pin_4, R2.Pin_0
  N3: S1.Pin_1, S1.Pin_2, R3.Pin_0, S2.Pin_1, S2.Pin_2, R6.Pin_0, S3.Pin_1, S3.Pin_2, S4.Pin_1, S4.Pin_2, R11.Pin_0, R12.Pin_0, LED4.anode, DIN1.2, Bauteil2.GND
  N4: R2.Pin_1, Bauteil2.D12/MISO
  N5: R3.Pin_1, LED1.cathode
  N6: LED1.anode, Bauteil2.D5
  N7: R4.Pin_1, S2.Pin_3, S2.Pin_4, R5.Pin_0
  N8: R5.Pin_1, Bauteil2.D11/MOSI
  N9: R6.Pin_1, LED2.cathode
  N10: LED2.anode, Bauteil2.D4
  N11: R7.Pin_1, S4.Pin_3, S4.Pin_4, R9.Pin_0
  N12: R8.Pin_1, S3.Pin_3, S3.Pin_4, R10.Pin_0
  N13: R9.Pin_1, Bauteil2.D9
  N14: R10.Pin_1, Bauteil2.D10
  N15: R11.Pin_1, LED4.cathode
  N16: R12.Pin_1, LED3.cathode
  N17: LED3.anode, Bauteil2.D3
  N18: DIN1.5, Bauteil2.D1/TX
  N19: DIN1.4, R13.Pin_0

notes:
  Front View
